// Logisim project Arithmetic_and_Logic_unit.circ as structural Verilog
module addersubber (
  input  Cin,
  input  [7:0] A,
  input  AS,
  input  [7:0] B,
  output [7:0] ADDout,
  output Cout,
  output OVout,
  output ACout,
  output [7:0] SUBout
);

  wire adder_1_cout, adder_2_cout, bitselector_1_out, bitselector_2_out, demultiplexer_1_out0,
       demultiplexer_1_out1, multiplexer_1_out, subtractor_1_bout, subtractor_2_bout, xnor_1_out, xor_1_out,
       xor_2_out;

  Demultiplexer demultiplexer_1 (.out0(demultiplexer_1_out0), .out1(demultiplexer_1_out1), .in(Cin), .sel(AS));
  Adder #(.width(4)) adder_1 (
    .a(A[3:0]), .b(B[3:0]), .out(ADDout[3:0]), .cin(demultiplexer_1_out0), .cout(adder_1_cout));
  Subtractor #(.width(4)) subtractor_1 (
    .a(A[3:0]), .b(B[3:0]), .out(SUBout[3:0]), .bin(demultiplexer_1_out1), .bout(subtractor_1_bout));
  xor xor_1 (xor_1_out, multiplexer_1_out, A[7]);
  xor xor_2 (xor_2_out, B[7], AS);
  Multiplexer multiplexer_1 (.in0(bitselector_1_out), .in1(bitselector_2_out), .out(multiplexer_1_out), .sel(AS));
  Adder #(.width(4)) adder_2 (.a(A[7:4]), .b(B[7:4]), .out(ADDout[7:4]), .cin(adder_1_cout), .cout(adder_2_cout));
  Subtractor #(.width(4)) subtractor_2 (
    .a(A[7:4]), .b(B[7:4]), .out(SUBout[7:4]), .bin(subtractor_1_bout), .bout(subtractor_2_bout));
  xnor xnor_1 (xnor_1_out, A[7], xor_2_out);
  Multiplexer multiplexer_2 (.in0(adder_2_cout), .in1(subtractor_2_bout), .out(Cout), .sel(AS));
  Multiplexer multiplexer_3 (.in0(adder_1_cout), .in1(subtractor_1_bout), .out(ACout), .sel(AS));
  and and_1 (OVout, xor_1_out, xnor_1_out);
  BitSelector bitselector_1 (.in(ADDout), .out(bitselector_1_out), .sel(3'b111));
  BitSelector bitselector_2 (.in(SUBout), .out(bitselector_2_out), .sel(3'b111));
endmodule

module ALU (
  input  Mode,
  input  [3:0] Operation,
  input  [7:0] Ain,
  input  [7:0] Bin,
  input  Cin,
  output [7:0] Result,
  output [7:0] Flags
);

  wire and_1_out, comparator_1_lt, undriven_10;
  wire [3:0] bitadder_1_out;
  wire [7:0] addersubber_1_addout, addersubber_1_subout, and_2_out, buffer_1_out, buffer_2_out,
       divider_1_out, divider_1_rem, multiplexer_1_out, multiplexer_3_out, multiplier_1_cout,
       multiplier_1_out, nand_1_out, negator_1_out, nor_1_out, not_1_out, not_2_out, or_1_out, shifter_1_out,
       shifter_2_out, shifter_3_out, shifter_4_out, shifter_5_out, undriven, undriven_2, undriven_3,
       undriven_4, undriven_5, undriven_6, undriven_7, undriven_8, undriven_9, xnor_1_out, xor_1_out;

  // NoConnect on Bin[7]
  // NoConnect on Bin[6]
  // NoConnect on Bin[5]
  // NoConnect on Bin[4]
  // NoConnect on Bin[3]
  and and_1 (and_1_out, ~Operation[3], ~Operation[2], Operation[0], ~Operation[1]);  // AND_Gate
  assign buffer_1_out = Ain;  // Buffer buffer_1, 8 bits wide
  assign buffer_2_out = Bin;  // Buffer buffer_2, 8 bits wide
  addersubber addersubber_1 (
    .AS(and_1_out), .Cin(Cin), .A(Ain), .B(Bin), .SUBout(addersubber_1_subout),
    .ADDout(addersubber_1_addout), .Cout(Flags[5]), .OVout(Flags[6]), .ACout(Flags[4]));
  Multiplier multiplier_1 (.a(Ain), .b(Bin), .out(multiplier_1_out), .cin({8{1'b0}}), .cout(multiplier_1_cout));
  Divider divider_1 (.a(Ain), .b(Bin), .out(divider_1_out), .upper({8{1'b0}}), .rem(divider_1_rem));
  Negator negator_1 (.in(Ain), .out(negator_1_out));
  Shifter shifter_1 (.in(Ain), .\dist (Bin[2:0]), .out(shifter_1_out));
  Shifter #(.shift("lr")) shifter_2 (.in(Ain), .\dist (Bin[2:0]), .out(shifter_2_out));
  Shifter #(.shift("ar")) shifter_3 (.in(Ain), .\dist (Bin[2:0]), .out(shifter_3_out));
  Shifter #(.shift("rl")) shifter_4 (.in(Ain), .\dist (Bin[2:0]), .out(shifter_4_out));
  Shifter #(.shift("rr")) shifter_5 (.in(Ain), .\dist (Bin[2:0]), .out(shifter_5_out));
  BitAdder bitadder_1 (.in0(Ain), .out(bitadder_1_out));
  assign not_1_out = ~Ain;  // NOT_Gate not_1, 8 bits wide
  assign not_2_out = ~Bin;  // NOT_Gate not_2, 8 bits wide
  assign and_2_out = Ain & Bin;  // AND_Gate and_2, 8 bits wide
  assign nand_1_out = ~(Ain & Bin);  // NAND_Gate nand_1, 8 bits wide
  assign or_1_out = Ain | Bin;  // OR_Gate or_1, 8 bits wide
  assign nor_1_out = ~(Ain | Bin);  // NOR_Gate nor_1, 8 bits wide
  assign xor_1_out = Ain ^ Bin;  // XOR_Gate xor_1, 8 bits wide
  assign xnor_1_out = ~(Ain ^ Bin);  // XNOR_Gate xnor_1, 8 bits wide
  Comparator comparator_1 (.a(Ain), .b(Bin), .gt(Flags[2]), .eq(Flags[3]), .lt(comparator_1_lt));
  // NoConnect on comparator_1_lt
  // NoConnect on undriven
  // NoConnect on undriven_2
  // NoConnect on undriven_3
  // NoConnect on undriven_4
  // NoConnect on undriven_5
  // NoConnect on undriven_6
  // NoConnect on undriven_7
  // NoConnect on undriven_8
  // NoConnect on undriven_9
  // NoConnect on undriven_10
  Multiplexer #(.select(4), .width(8)) multiplexer_1 (
    .in0(addersubber_1_addout), .in1(addersubber_1_subout), .in2(multiplier_1_out), .in3(multiplier_1_cout),
    .in4(divider_1_out), .in5(divider_1_rem), .in6(negator_1_out), .in7(shifter_3_out),
    .in8({4'b0000, bitadder_1_out}), .in9(buffer_1_out), .in10(buffer_2_out), .in11(undriven),
    .in12(undriven_2), .in13(undriven_3), .in14(undriven_4), .in15(undriven_5), .out(multiplexer_1_out),
    .sel(Operation));
  Multiplexer #(.width(8)) multiplexer_2 (
    .in0(multiplexer_1_out), .in1(multiplexer_3_out), .out({Flags[7], Result[6:0]}), .sel(Mode));
  Multiplexer #(.select(4), .width(8)) multiplexer_3 (
    .in0(shifter_1_out), .in1(shifter_2_out), .in2(shifter_4_out), .in3(shifter_5_out), .in4(not_1_out),
    .in5(not_2_out), .in6(and_2_out), .in7(nand_1_out), .in8(or_1_out), .in9(nor_1_out), .in10(xor_1_out),
    .in11(xnor_1_out), .in12(undriven_6), .in13(undriven_7), .in14(undriven_8), .in15(undriven_9),
    .out(multiplexer_3_out), .sel(Operation));
  xor parity (Flags[1], Flags[7], Result[6], Result[5], Result[4], Result[3], Result[2], Result[1], Result[0]);
  and zero (Flags[0], ~Flags[7], ~Result[6], ~Result[5], ~Result[4], ~Result[2], ~Result[1], ~Result[0], ~Result[3]);  // AND_Gate

  assign Result[7] = Flags[7];

  // Notes on the sheet:
  //   Arithmetic
  //   Logic
  //   Note:
  //   If any operations other than add or sub is performed. these flags are set 
  //   add and sub operations
  //   Flags:[S|OV|C|AC|EQ|GT|P|Z]
  //   The C,AC,OV flags only update for addition and subtraction operations,
  //   based on addition of those two operands.  In short use these flags only for
endmodule
