// Logisim project pipeline.circ as structural Verilog
module FetchUnit (
  input  [7:0] instrORimm,
  input  clk,
  input  reset,
  input  delayIN,
  input  stall,
  output [1:0] count,
  output [7:0] pipelineRegisters,
  output [7:0] pipeline,
  output delayOUT,
  output ready,
  output incPC,
  output [7:0] fetchReg
);

  wire and_1_out, nor_1_out, or_1_out, register_1_q;
  wire [7:0] multiplexer_1_out;

  Multiplexer #(.width(8)) multiplexer_1 (.in0({8{1'b0}}), .in1(instrORimm), .out(multiplexer_1_out), .sel(1'b1));
  // Probe on instrORimm
  // NoConnect on multiplexer_1_out[0]
  // NoConnect on multiplexer_1_out[1]
  // NoConnect on multiplexer_1_out[2]
  // NoConnect on multiplexer_1_out[3]
  // NoConnect on multiplexer_1_out[4]
  // NoConnect on multiplexer_1_out[5]
  Register #(.width(1)) register_1 (.D(nor_1_out), .en(1'b1), .clk(clk), .Q(register_1_q), .clr(reset));
  Register register_2 (.D(instrORimm), .en(1'b1), .clk(clk), .Q(fetchReg), .clr(reset));
  or or_1 (or_1_out, multiplexer_1_out[6], multiplexer_1_out[7]);
  and and_1 (and_1_out, or_1_out, nor_1_out);
  nor nor_1 (nor_1_out, count[0], count[1]);
  Counter #(.max('h3), .ongoal("stay"), .width(2)) counter_1 (
    .load(and_1_out), .D(multiplexer_1_out[7:6]), .count(1'b1), .Q(count), .up(1'b0), .clk(clk), .clr(reset));  // open: carry
  Demultiplexer #(.width(8)) demultiplexer_1 (
    .out0(pipelineRegisters), .out1(pipeline), .in(fetchReg), .sel(register_1_q));
  and and_2 (ready, register_1_q, 1'b1);

  assign delayOUT = 1'b1;
  assign incPC = 1'b1;

  // Notes on the sheet:
  //   Note: Ready signal is not meant for enabling the write input, it is to say all the
  //   immediate values are loaded into the pipeline registers to the decode units
  //   currently it is being used for write enable and must be changed in the future
endmodule

module delay (
  input  dIN,
  input  clock,
  input  reset,
  output dOUT,
  output ss
);

  wire d_ff_1_qn, d_ff_2_qn, undriven, undriven_2;

  D_Flip_Flop d_ff_1 (.D(dIN), .clk(clock), .Q(ss), .Qn(d_ff_1_qn), .preset(undriven), .reset(reset));
  // NoConnect on undriven
  D_Flip_Flop d_ff_2 (.D(ss), .clk(clock), .Q(dOUT), .Qn(d_ff_2_qn), .preset(undriven_2), .reset(reset));
  // NoConnect on d_ff_1_qn
  // NoConnect on undriven_2
  // NoConnect on d_ff_2_qn
endmodule

module test2 (
  input  load,
  input  [15:0] FFFFin,
  input  rst,
  output [7:0] PipelineRegisters,
  output [7:0] nextStage
);

  wire clk_out, fetchunit_1_delayout, fetchunit_1_incpc, fetchunit_1_ready;
  wire [1:0] fetchunit_1_count;
  wire [7:0] fetchunit_1_fetchreg, fetchunit_1_pipeline, fetchunit_1_pipelineregisters, register_1_q,
       register_2_q, register_3_q, register_4_q, rom_1_data;
  wire [15:0] programcounter_1_ffffout;

  ROM #(.addrWidth(16)) rom_1 (.addr(programcounter_1_ffffout), .data(rom_1_data));
  ProgramCounter programcounter_1 (
    .FFFFin(FFFFin), .enable(fetchunit_1_incpc), .load(load), .clock(clk_out), .reset(rst),
    .FFFFout(programcounter_1_ffffout));
  // Probe on rom_1_data
  Clock clk (.out(clk_out));
  // Probe on fetchunit_1_fetchreg
  // Probe on fetchunit_1_count
  FetchUnit fetchunit_1 (
    .instrORimm(rom_1_data), .clk(clk_out), .reset(rst), .count(fetchunit_1_count),
    .pipelineRegisters(fetchunit_1_pipelineregisters), .pipeline(fetchunit_1_pipeline),
    .delayOUT(fetchunit_1_delayout), .ready(fetchunit_1_ready), .incPC(fetchunit_1_incpc),
    .fetchReg(fetchunit_1_fetchreg));  // open: delayIN, stall
  Register register_1 (
    .D(fetchunit_1_pipelineregisters), .en(fetchunit_1_delayout), .clk(clk_out), .Q(register_1_q), .clr(rst));
  Register register_2 (.D(fetchunit_1_pipeline), .en(fetchunit_1_ready), .clk(clk_out), .Q(register_2_q), .clr(rst));
  Register register_3 (.D(register_1_q), .en(fetchunit_1_delayout), .clk(clk_out), .Q(register_3_q), .clr(rst));
  Register register_4 (.D(register_2_q), .en(fetchunit_1_ready), .clk(clk_out), .Q(register_4_q), .clr(rst));
  Register register_5 (.D(register_3_q), .en(fetchunit_1_delayout), .clk(clk_out), .Q(PipelineRegisters), .clr(rst));
  Register register_6 (.D(register_4_q), .en(fetchunit_1_ready), .clk(clk_out), .Q(nextStage), .clr(rst));

  // Notes on the sheet:
  //   contents of rom_1 (hex, n*v repeats v):
  //   73 8e 74 19 94 ea d1 9b 31 93 1c fe 1f 3b c 9a 4d f3 46 6d 4 7c 9a e4 3f f9 f 54 6f ab a2 73 1d 7 4
  //   22 87 c0 64 8b 93 90 91 fa cb f2 5 88 53 94 eb 17 4a b3 19 f7 8c a9 ae 12 e6 f4 93 89 7e 53 52 bc 54
  //   9 20 a3 b8 1d aa 2d 1b 99 79 94 73 13 18 56 82 a8 7f fa 84 fe cb 7c 52 39 ee 82 db b 7f 6f 6c 3a e9
  //   6 3c ba 73 53 70 34 a0 39 4e b0 5e bf cd be 56 c1 d8 9d c9 df ad 6f f1 28 4e 4a 7f b8 51 e4 48 66 65
  //   1e 56 dd 94 ec da 48 3d b3 f1 7d e 1f 49 af 5 50 95 da 52 5f 4a 1 3 68 a5 12 73 5 fb d3 c9 27 60 ed
  //   ca 7b 28 71 c6 a4 60 53 b1 65 4a 2c c5 a1 f3 42 66 51 ea 57 f4 57 39 65 a4 3 9e 5b c9 df 58 2 4 82 d
  //   32 c0 b1 5b 6c aa 2 2e 4f 4d c7 b5 d9 b1 9 27 6e 1a 89 bf f0 f5 cf 91 dc 1b 1a f7 7e 1c 2f 9b b5 a8
  //   d9 65 e 29 15 4d a2 3f e1 f3 39 4a f6 53 8b c7 85 ae 49 46 3e e b0 cf 52 81 6a 1 af fd b6 1 87 54 eb
  //   2d 2d a bc 35 11 73 8 b7 7b 5d cc 9b 59 55 47 63 a8 cb 14 63 c9 b 49 b9 8b 25 9b 6d 34 80 48 17 83
  //   20 57 4c 25 5a 24 3f 35 0 eb 16 b6 17 5f e3 93 d 78 30 22 59 5 91 c3 fb 6c 4c 45 64 e9 86 da 5 c1 7d
  //   70 16 8f 79 8c dc af d4 6e d4 63 f6 85 9a 16 92 1c c3 e4 30 a6 bb e4 6f 4c 70 4d b0 2b 27 5f e3 25
  //   3e 87 1e 75 f6 89 19 7b 66 71 ab b8 97 b7 79 5c 20 c8 87 64 f 1b be c9 40 4a 95 57 df a2 48 d3 b3 bc
  //   24 af 4a 4d c0 9c 68 e0 45 7e a5 af 25 8e fc a6 67 81 a1 f5 b0 af 84 1e 7f 5 9a 22 60 9e 88 2b 2 b4
  //   38 2c 23 b9 62 9a 3b 76 6f f5 2e f1 e4 7f 45 10 ca 93 13 37 12 35 32 72 c9 2b 4c 1f 9d fe 8c 38 30
  //   99 21 9f 8a cb f2 f3 fd c6 db 9a b2 4b 1 8d 5c f0 66 5f f d8 36 aa 64 b5 f6 89 6 be 9f 3f fd 1 b3 1d
  //   7d c6 a6 d0 4a fb fc 76 a9 1d f3 5 c8 3b 14 93 b1 f1 a2 6b 43 7f d8 1d 56 c9 ef 81 85 c7 45 23 75 2b
  //   f5 51 4a ee f6 60 14 4f be 56 1e 15 89 cb 4a c9 13 5d 4b be 62 20 d3 8c c2 d0 a7 18 5e c b6 79 90 c1
  //   3c d0 44 3a 16 20 cc b7 a2 ec 92 8b b6 1a 49 a7 57 55 72 e3 cc 1f f5 87 51 42 d9 2e e5 83 f9 d ac 52
  //   87 e7 db a8 45 8f 15 39 cc 9a 55 4 da d3 11 66 88 83 d3 c 60 dc 63 98 9f e 76 dd 82 1e 6b b0 fc ee
  //   e9 7a c e8 ae bd 54 31 37 91 1f fa 72 82 fb d4 22 33 62 ae bf ac 11 49 61 c8 5e 7d 3c b1 1d 8f b0 2
  //   cb 74 9e 8f 27 47 a7 9d 44 d9 68 26 75 8a 44 aa 7d 5 71 7a c0 42 96 c8 d1 f4 d5 e6 23 7e 9 30 77 43
  //   ef ed c8 15 59 8f bb 60 1e a6 8c d8 45 5b 26 eb 71 e3 f0 9f 3e c8 ac 6d 97 3c f0 ac 5c a7 4 bf 92 eb
  //   9d a9 bd 5f de 6b 21 c0 fa 69 9d 97 1d b8 bf 1 f9 af f7 4f 8a 74 2d 4a 2c 12 47 c2 cf ea 7e 9a e3 80
  //   86 13 f3 48 65 ff 51 f 73 c8 a1 bb 20 3f d7 5a 9e dc 6a 0 21 7e ae 80 36 47 3f e5 64 a6 91 94 43 32
  //   9f de 4c 36 5 ac df 7 ec a5 f0 d6 5b 82 34 7 48 a 82 93 2a 0 76 86 cb 11 f6 ae 3 31 32 eb 80 bc d2
  //   fc 35 c 11 30 12 c0 df 57 84 31 b2 90 23 62 62 3f 2 37 1e 94 a aa 7d 40 22 6f 66 49 95 5a da 6b 86
  //   7c d4 49 6 2a 37 27 b5 53 7 37 7 ce d8 df 94 11 51 fb 21 1e d3 f9 a2 29 3a fe 1a 73 84 4c d6 aa d d
  //   aa 20 80 74 ed 8d b4 6b 6a 62 93 f2 27 df 80 cf 6c 79 60 e1 cb 9a a1 a7 3c 64 59 13 ad 5e 81 de cf
  //   4f 67 2c 24 3a 2e c9 3d 52 9d b6 fc 3c ee e3 ed c3 a2 63 b2 ab 80 2f cf f da 13 83 99 22 74 ce 8 23
  //   eb 41 c9 b6 d6 ea 8d 9f f5 6a 55 e2 46 83 19 f2 bf ee d3 39 26 f 1b 96 af d4 b1 41 2a 73 ef 97 14 d
  //   31 23 69 3 92 b7 c8 fb 2f a4 7e e6 67 e2 68 84 89 c2 28 53 df e5 31 1e a5 99 9c 89 6d 1c b7 2a 4b 50
  //   66 4f f0 b1 5d d5 1d b3 a0 72 f3 3 7c d5 e7 f1 a4 bc 72 e 2d 6e bb dc dd d5 f9 36 cb dc 5b 8d c0 dc
  //   e4 15 24 c9 86 8a 7e ea 97 54 1f 44 fd c9 71 6d 4a 1d d0 23 1e 73 d9 d5 f0 d5 db 81 80 16 1a 91 78
  //   e1 84 56 57 6e e9 5a 2d a9 85 3c f8 ff 7f 3f 2c 89 c6 d9 35 a7 32 28 86 f4 f 78 4c 22 f1 c8 64 24 ff
  //   61 fc 6b d3 dc a4 c0 57 2f ee 8d 17 dd cb 52 b7 3e a7 4e 27 24 3b 82 a8 14 5e d3 70 e6 a2 f8 88 1c
  //   54 e0 dc 2a 38 33 72 24 43 ec 77 33 bc 6d e3 a7 e7 f1 d2 b7 ff 9a c4 f9 1c d7 2a 8d bc 2a d3 3 1c 81
  //   55 f7 88 df 7 8 c5 8d 8a c8 aa ee 5b 74 74 59 f9 84 38 49 b5 6d 8 a2 46 bc 6 5c 95 3 f5 48 db 5c 13
  //   f1 c9 ff 32 30 97 de cb 41 4 76 68 1a 3c 3b c8 e0 30 6e a1 8 b8 96 e0 9 b0 29 6a 0 58 eb 7f a6 96 4d
  //   65 37 16 50 a6 1d b8 f2 f1 de fe 6b 46 4f d2 b0 c2 5f 2 a4 8d c1 29 38 51 5e a1 d5 eb d6 a5 2b 51 c4
  //   c2 76 a9 9f 49 d5 13 6f a7 fd 15 6e 40 a6 a4 a8 c0 3b 98 33 f0 39 a0 42 53 1d 25 e6 be f5 c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
endmodule

module test1 (
  input  [7:0] instrORimm,
  input  clk,
  input  reset,
  input  delayIn,
  input  insertNOPE,
  output [7:0] PipelineRegisters,
  output [7:0] nextStage,
  output ready,
  output incPC
);

  wire and_1_out, and_2_out, c, or_1_out, or_2_out, register_1_q, t_ff_1_q, t_ff_1_qn;
  wire [1:0] counter_1_q;
  wire [7:0] demultiplexer_1_out0, demultiplexer_1_out1, multiplexer_1_out, register_2_q, register_3_q,
       register_4_q, register_5_q, register_6_q;

  Multiplexer #(.width(8)) multiplexer_1 (.in0({8{1'b0}}), .in1(instrORimm), .out(multiplexer_1_out), .sel(delayIn));
  // NoConnect on multiplexer_1_out[0]
  // NoConnect on multiplexer_1_out[1]
  // NoConnect on multiplexer_1_out[2]
  // NoConnect on multiplexer_1_out[3]
  // NoConnect on multiplexer_1_out[4]
  // NoConnect on multiplexer_1_out[5]
  Register #(.width(1)) register_1 (.D(c), .en(delayIn), .clk(clk), .Q(register_1_q), .clr(reset));
  or or_1 (or_1_out, delayIn, c);
  // NOT_Gate not_1 has open pins: in=insertNOPE, out=open
  or or_2 (or_2_out, multiplexer_1_out[6], multiplexer_1_out[7]);
  and and_1 (and_1_out, or_2_out, c);
  nor nor_1 (c, counter_1_q[0], counter_1_q[1]);
  Register register_2 (.D(instrORimm), .en(delayIn), .clk(clk), .Q(register_2_q), .clr(reset));
  // NOT_Gate not_2 has open pins: in=t_ff_1_q, out=open
  T_Flip_Flop t_ff_1 (.T(or_1_out), .clk(clk), .Q(t_ff_1_q), .Qn(t_ff_1_qn), .reset(reset), .preset(1'b0));
  // NoConnect on t_ff_1_qn
  Counter #(.max('h3), .ongoal("stay"), .width(2)) counter_1 (
    .load(and_1_out), .D(multiplexer_1_out[7:6]), .count(delayIn), .Q(counter_1_q), .up(1'b0), .clk(clk),
    .clr(reset));  // open: carry
  Demultiplexer #(.width(8)) demultiplexer_1 (
    .out0(demultiplexer_1_out0), .out1(demultiplexer_1_out1), .in(register_2_q), .sel(register_1_q));
  and and_2 (and_2_out, register_1_q, delayIn);
  Register register_3 (.D(demultiplexer_1_out0), .en(delayIn), .clk(clk), .Q(register_3_q), .clr(reset));
  Register register_4 (.D(demultiplexer_1_out1), .en(and_2_out), .clk(clk), .Q(register_4_q), .clr(reset));
  Register register_5 (.D(register_3_q), .en(delayIn), .clk(clk), .Q(register_5_q), .clr(reset));
  Register register_6 (.D(register_4_q), .en(and_2_out), .clk(clk), .Q(register_6_q), .clr(reset));
  Register register_7 (.D(register_5_q), .en(delayIn), .clk(clk), .Q(PipelineRegisters), .clr(reset));
  Register register_8 (.D(register_6_q), .en(and_2_out), .clk(clk), .Q(nextStage), .clr(reset));

  // Notes on the sheet:
  //   delay is used for requesting the pipeline to halt the next cycle 
  //   and it is not meant for handling pipeline hazards
endmodule

module decodeUnit (
  input  [7:0] pipelineReg1,
  input  [7:0] pipelineReg2,
  input  [7:0] pipelineReg3,
  input  [7:0] pipelineIn,
  input  ready,
  input  [15:0] in_6,
  input  clk,
  input  rst,
  output [3:0] regA,
  output [3:0] regB,
  output [3:0] operation,
  output [3:0] regRes,
  output [7:0] pipelineOut,
  output ALUmode,
  output Cin
);

  wire [15:0] controlROM_data;
  wire [15:2] multiplexer_1_out;

  // NoConnect on pipelineReg3
  Register register_1 (.D(pipelineIn), .en(ready), .clk(clk), .Q(pipelineOut), .clr(rst));
  // NoConnect on pipelineOut[7]
  // NoConnect on pipelineOut[6]
  ROM #(.addrWidth(6), .dataWidth(16)) controlROM (.addr(pipelineOut[5:0]), .data(controlROM_data));
  // Probe on in_6
  Multiplexer #(.width(16)) multiplexer_1 (
    .in0({16{1'b0}}), .in1(controlROM_data), .out({multiplexer_1_out, Cin, ALUmode}), .sel(ready));
  // NoConnect on multiplexer_1_out[2]
  // NoConnect on multiplexer_1_out[3]
  // NoConnect on multiplexer_1_out[4]
  // NoConnect on multiplexer_1_out[5]
  // NoConnect on multiplexer_1_out[6]
  // NoConnect on multiplexer_1_out[7]
  // NoConnect on multiplexer_1_out[8]
  // NoConnect on multiplexer_1_out[9]
  // NoConnect on multiplexer_1_out[10]
  // NoConnect on multiplexer_1_out[11]
  // NoConnect on multiplexer_1_out[12]
  // NoConnect on multiplexer_1_out[13]
  // NoConnect on multiplexer_1_out[14]
  // NoConnect on multiplexer_1_out[15]

  assign operation = pipelineReg2[3:0];
  assign regA = pipelineReg1[3:0];
  assign regB = pipelineReg1[7:4];
  assign regRes = pipelineReg2[7:4];

  // Notes on the sheet:
  //   contents of controlROM (hex, n*v repeats v):
  //   4*0 2 15*0 30*1
  //   Note: implement Ready signal it is not just a write enable signal it must only decode and execute instruction when on
endmodule
