// Logisim project registers_and_memory.circ as structural Verilog
module GeneralPurposeRegisters (
  input  [2:0] write_Addr,
  input  [2:0] A_addr,
  input  [7:0] data,
  input  reset,
  input  clock,
  input  [2:0] B_addr,
  output [7:0] A,
  output [7:0] B
);

  wire decoder_1_out0, decoder_1_out1, decoder_1_out2, decoder_1_out3, decoder_1_out4, decoder_1_out5,
       decoder_1_out6, decoder_1_out7, decoder_2_out0, decoder_2_out1, decoder_2_out2, decoder_2_out3,
       decoder_2_out4, decoder_2_out5, decoder_2_out6, decoder_2_out7, decoder_3_out0, decoder_3_out1,
       decoder_3_out2, decoder_3_out3, decoder_3_out4, decoder_3_out5, decoder_3_out6, decoder_3_out7;
  wire [7:0] register_1_q, register_2_q, register_3_q, register_4_q, register_5_q, register_6_q,
       register_7_q, register_8_q, register_9_q, register_10_q, register_11_q, register_12_q, register_13_q,
       register_14_q, register_15_q, register_16_q;

  Decoder #(.enable("false"), .select(3)) decoder_1 (
    .out0(decoder_1_out0), .out1(decoder_1_out1), .out2(decoder_1_out2), .out3(decoder_1_out3),
    .out4(decoder_1_out4), .out5(decoder_1_out5), .out6(decoder_1_out6), .out7(decoder_1_out7),
    .sel(write_Addr));
  Decoder #(.enable("false"), .select(3)) decoder_2 (
    .out0(decoder_2_out0), .out1(decoder_2_out1), .out2(decoder_2_out2), .out3(decoder_2_out3),
    .out4(decoder_2_out4), .out5(decoder_2_out5), .out6(decoder_2_out6), .out7(decoder_2_out7), .sel(A_addr));
  Decoder #(.enable("false"), .select(3)) decoder_3 (
    .out0(decoder_3_out0), .out1(decoder_3_out1), .out2(decoder_3_out2), .out3(decoder_3_out3),
    .out4(decoder_3_out4), .out5(decoder_3_out5), .out6(decoder_3_out6), .out7(decoder_3_out7), .sel(B_addr));
  Register register_1 (.D(data), .en(decoder_1_out0), .clk(clock), .Q(register_1_q), .clr(reset));
  Register register_2 (.D(data), .en(decoder_1_out0), .clk(clock), .Q(register_2_q), .clr(reset));
  assign A = decoder_2_out0 ? register_1_q : 8'bz;  // Controlled_Buffer controlled_buffer_1
  assign B = decoder_3_out0 ? register_2_q : 8'bz;  // Controlled_Buffer controlled_buffer_2
  Register register_3 (.D(data), .en(decoder_1_out1), .clk(clock), .Q(register_3_q), .clr(reset));
  Register register_4 (.D(data), .en(decoder_1_out1), .clk(clock), .Q(register_4_q), .clr(reset));
  assign A = decoder_2_out1 ? register_3_q : 8'bz;  // Controlled_Buffer controlled_buffer_3
  Register register_5 (.D(data), .en(decoder_1_out2), .clk(clock), .Q(register_5_q), .clr(reset));
  Register register_6 (.D(data), .en(decoder_1_out2), .clk(clock), .Q(register_6_q), .clr(reset));
  assign B = decoder_3_out1 ? register_4_q : 8'bz;  // Controlled_Buffer controlled_buffer_4
  assign A = decoder_2_out2 ? register_5_q : 8'bz;  // Controlled_Buffer controlled_buffer_5
  assign B = decoder_3_out2 ? register_6_q : 8'bz;  // Controlled_Buffer controlled_buffer_6
  Register register_7 (.D(data), .en(decoder_1_out3), .clk(clock), .Q(register_7_q), .clr(reset));
  Register register_8 (.D(data), .en(decoder_1_out3), .clk(clock), .Q(register_8_q), .clr(reset));
  assign A = decoder_2_out3 ? register_7_q : 8'bz;  // Controlled_Buffer controlled_buffer_7
  Register register_9 (.D(data), .en(decoder_1_out4), .clk(clock), .Q(register_9_q), .clr(reset));
  Register register_10 (.D(data), .en(decoder_1_out4), .clk(clock), .Q(register_10_q), .clr(reset));
  assign B = decoder_3_out3 ? register_8_q : 8'bz;  // Controlled_Buffer controlled_buffer_8
  assign A = decoder_2_out4 ? register_9_q : 8'bz;  // Controlled_Buffer controlled_buffer_9
  assign B = decoder_3_out4 ? register_10_q : 8'bz;  // Controlled_Buffer controlled_buffer_10
  Register register_11 (.D(data), .en(decoder_1_out5), .clk(clock), .Q(register_11_q), .clr(reset));
  Register register_12 (.D(data), .en(decoder_1_out5), .clk(clock), .Q(register_12_q), .clr(reset));
  assign A = decoder_2_out5 ? register_11_q : 8'bz;  // Controlled_Buffer controlled_buffer_11
  Register register_13 (.D(data), .en(decoder_1_out6), .clk(clock), .Q(register_13_q), .clr(reset));
  Register register_14 (.D(data), .en(decoder_1_out6), .clk(clock), .Q(register_14_q), .clr(reset));
  assign B = decoder_3_out5 ? register_12_q : 8'bz;  // Controlled_Buffer controlled_buffer_12
  assign A = decoder_2_out6 ? register_13_q : 8'bz;  // Controlled_Buffer controlled_buffer_13
  assign B = decoder_3_out6 ? register_14_q : 8'bz;  // Controlled_Buffer controlled_buffer_14
  Register register_15 (.D(data), .en(decoder_1_out7), .clk(clock), .Q(register_15_q), .clr(reset));
  Register register_16 (.D(data), .en(decoder_1_out7), .clk(clock), .Q(register_16_q), .clr(reset));
  assign A = decoder_2_out7 ? register_15_q : 8'bz;  // Controlled_Buffer controlled_buffer_15
  assign B = decoder_3_out7 ? register_16_q : 8'bz;  // Controlled_Buffer controlled_buffer_16

  // Notes on the sheet:
  //   add reset and the decoders will output 0 in all lines
endmodule

module SpecialFunctionRegisters (
  input  [2:0] RegSelect,
  input  [15:0] AddressIn,
  input  [7:0] Flags,
  input  [7:0] SystemCalls,
  input  [7:0] returnBytes,
  input  reset,
  input  clock,
  input  load,
  input  INCdec,
  input  RETtoPC,
  output [15:0] DataMemAddr,
  output [15:0] InstrMemAddr,
  output [7:0] Status,
  output [7:0] SysCalls,
  output [7:0] Luckaton
);

  wire decoder_1_out0, decoder_1_out1, decoder_1_out2, decoder_1_out3, decoder_1_out4, decoder_1_out5,
       decoder_1_out6, decoder_1_out7;
  wire [7:0] RNG_out, StatusRegister_q;
  wire [15:0] multiplexer_1_out, returnregister_1_ffffout;

  Decoder #(.enable("false"), .select(3)) decoder_1 (
    .out0(decoder_1_out0), .out1(decoder_1_out1), .out2(decoder_1_out2), .out3(decoder_1_out3),
    .out4(decoder_1_out4), .out5(decoder_1_out5), .out6(decoder_1_out6), .out7(decoder_1_out7),
    .sel(RegSelect));
  Multiplexer #(.width(16)) multiplexer_1 (
    .in0(AddressIn), .in1(returnregister_1_ffffout), .out(multiplexer_1_out), .sel(RETtoPC));
  ReturnRegister returnregister_1 (
    .FFin(returnBytes), .enable(decoder_1_out7), .HBlb(load), .clock(clock), .reset(reset),
    .FFFFout(returnregister_1_ffffout));
  ProgramCounter programcounter_1 (
    .FFFFin(multiplexer_1_out), .enable(decoder_1_out6), .load(load), .clock(clock), .reset(reset),
    .FFFFout(InstrMemAddr));
  StackPointer stackpointer_1 (
    .FFFFin(AddressIn), .enable(decoder_1_out5), .popPUSH(INCdec), .load(load), .clock(clock), .reset(reset),
    .FFFFout(DataMemAddr));
  SourceIndex sourceindex_1 (
    .FFFFin(AddressIn), .enable(decoder_1_out4), .INCdec(INCdec), .load(load), .clock(clock), .reset(reset),
    .FFFFout(DataMemAddr));
  Register StatusRegister (.D(Flags), .en(decoder_1_out2), .clk(clock), .Q(StatusRegister_q), .clr(reset));
  DestinationIndex destinationindex_1 (
    .FFFFin(AddressIn), .enable(decoder_1_out3), .INCdec(INCdec), .load(load), .clock(clock), .reset(reset),
    .FFFFout(DataMemAddr));
  assign Status = decoder_1_out2 ? StatusRegister_q : 8'bz;  // Controlled_Buffer controlled_buffer_1
  Register SysRegister (.D(SystemCalls), .en(decoder_1_out1), .clk(clock), .Q(SysCalls), .clr(reset));
  Random RNG (.clr(reset), .next(decoder_1_out0), .clk(clock), .out(RNG_out));
  assign Luckaton = decoder_1_out0 ? RNG_out : 8'bz;  // Controlled_Buffer controlled_buffer_2
endmodule

module ProgramCounter (
  input  [15:0] FFFFin,
  input  enable,
  input  load,
  input  clock,
  input  reset,
  output [15:0] FFFFout
);

  wire counter_1_carry;
  wire [15:0] counter_1_q;

  Counter #(.max('hffff), .width(16)) counter_1 (
    .clr(reset), .load(load), .up(1'b1), .count(enable), .clk(clock), .D(FFFFin), .carry(counter_1_carry),
    .Q(counter_1_q));
  // NoConnect on counter_1_carry
  assign FFFFout = enable ? counter_1_q : 16'bz;  // Controlled_Buffer controlled_buffer_1
endmodule

module ReturnRegister (
  input  [7:0] FFin,
  input  enable,
  input  HBlb,
  input  clock,
  input  reset,
  output [15:0] FFFFout
);

  wire not_1_out;
  wire [7:0] controlled_buffer_1_out, register_1_q;

  assign controlled_buffer_1_out = enable ? FFin : 8'bz;  // Controlled_Buffer controlled_buffer_1
  Register register_1 (.D(controlled_buffer_1_out), .en(HBlb), .clk(clock), .Q(register_1_q), .clr(reset));
  not not_1 (not_1_out, HBlb);
  Register #(.width(16)) register_2 (
    .D({register_1_q, controlled_buffer_1_out}), .en(not_1_out), .clk(clock), .Q(FFFFout), .clr(reset));
endmodule

module StackPointer (
  input  [15:0] FFFFin,
  input  enable,
  input  popPUSH,
  input  load,
  input  clock,
  input  reset,
  output [15:0] FFFFout
);

  wire counter_1_carry;
  wire [15:0] counter_1_q, not_1_out, not_2_out;

  assign not_1_out = ~FFFFin;  // NOT_Gate not_1, 16 bits wide
  Counter #(.max('hffff), .width(16)) counter_1 (
    .clr(reset), .load(load), .up(popPUSH), .count(enable), .clk(clock), .D(not_1_out),
    .carry(counter_1_carry), .Q(counter_1_q));
  // NoConnect on counter_1_carry
  assign not_2_out = ~counter_1_q;  // NOT_Gate not_2, 16 bits wide
  assign FFFFout = enable ? not_2_out : 16'bz;  // Controlled_Buffer controlled_buffer_1
endmodule

module SourceIndex (
  input  [15:0] FFFFin,
  input  enable,
  input  INCdec,
  input  load,
  input  clock,
  input  reset,
  output [15:0] FFFFout
);

  wire counter_1_carry;
  wire [15:0] counter_1_q;

  Counter #(.max('hffff), .width(16)) counter_1 (
    .clr(reset), .load(load), .up(INCdec), .count(enable), .clk(clock), .D(FFFFin), .carry(counter_1_carry),
    .Q(counter_1_q));
  // NoConnect on counter_1_carry
  assign FFFFout = enable ? counter_1_q : 16'bz;  // Controlled_Buffer controlled_buffer_1
endmodule

module DestinationIndex (
  input  [15:0] FFFFin,
  input  enable,
  input  INCdec,
  input  load,
  input  clock,
  input  reset,
  output [15:0] FFFFout
);

  wire counter_1_carry;
  wire [15:0] counter_1_q;

  Counter #(.max('hffff), .width(16)) counter_1 (
    .clr(reset), .load(load), .up(INCdec), .count(enable), .clk(clock), .D(FFFFin), .carry(counter_1_carry),
    .Q(counter_1_q));
  // NoConnect on counter_1_carry
  assign FFFFout = enable ? counter_1_q : 16'bz;  // Controlled_Buffer controlled_buffer_1
endmodule

module test (
  input  [3:0] in_1,
  input  [2:0] in_2,
  input  [2:0] in_3,
  input  [2:0] in_4,
  input  [7:0] in_5,
  input  in_6,
  input  in_7,
  output [3:0] out_8,
  output [7:0] out_9,
  output [7:0] out_10
);

  anotherfuckingtestvhdlentity anotherfuckingtestvhdlentity_1 (.val(in_1), .max(out_8));
  RegisterFile registerfile_1 (
    .A_addr(in_2), .B_addr(in_3), .Write_addr(in_4), .data(in_5), .reset(in_6), .clock(in_7),
    .A_output(out_9), .B_output(out_10));
endmodule

// VHDL entity RegisterFile, as the project stores it:
--------------------------------------------------------------------------------
-- Project :
-- File    :
-- Autor   :
-- Date    :
--
--------------------------------------------------------------------------------
-- Description :
--
--------------------------------------------------------------------------------

LIBRARY ieee;
USE ieee.std_logic_1164.all;
use ieee.NUMERIC_STD.all;

ENTITY RegisterFile IS
	port(
		----------------------------------------------------------------
		-- Inputs
		A_addr: in std_logic_vector(2 downto 0); -- 3-bit input
		B_addr: in std_logic_vector(2 downto 0); -- 3-bit input
		Write_addr: in std_logic_vector(2 downto 0); -- 3-bit input
		data: in std_logic_vector(7 downto 0);
		reset: in std_logic;
		clock: in std_logic;

		----------------------------------------------------------------
		-- Outputs
		A_output: out std_logic_vector(7 downto 0);
		B_output: out std_logic_vector(7 downto 0)
		);
END RegisterFile;



--------------------------------------------------------------------------------
--Complete your VHDL description below
--------------------------------------------------------------------------------

ARCHITECTURE TypeArchitecture OF RegisterFile IS
	type regArray is array(0 to 7) of STD_LOGIC_VECTOR(7 downto 0);
	signal regs: regArray  := (others => (others => '0'));
BEGIN
-- Write process
	process(clock,reset)
	begin
		if reset = '1' then
			regs <= (others => (others => '0'));
		elsif rising_edge(clock) then
			regs(to_integer(unsigned(Write_addr)))  <= data;
		end if;
	end process;

-- Read ports
	A_output  <=  regs(to_integer(unsigned(A_addr)));
	B_output  <=  regs(to_integer(unsigned(B_addr)));

END TypeArchitecture;

// VHDL entity anotherfuckingtestvhdlentity, as the project stores it:
--------------------------------------------------------------------------------
-- Project :
-- File    :
-- Autor   :
-- Date    :
--
--------------------------------------------------------------------------------
-- Description :
--
--------------------------------------------------------------------------------

LIBRARY ieee;
USE ieee.std_logic_1164.all;

ENTITY anotherfuckingtestvhdlentity IS
  PORT (
  ------------------------------------------------------------------------------
  --Insert input ports below
    val        : IN  std_logic_vector(3 DOWNTO 0); -- input vector example
  ------------------------------------------------------------------------------
  --Insert output ports below
    max        : OUT std_logic_vector(3 DOWNTO 0)  -- output vector example
    );
END anotherfuckingtestvhdlentity;

--------------------------------------------------------------------------------
--Complete your VHDL description below
--------------------------------------------------------------------------------

ARCHITECTURE TypeArchitecture OF anotherfuckingtestvhdlentity IS

BEGIN
	max  <= val;
END TypeArchitecture;
